// Logisim project circuito.circ as structural Verilog: 1 circuit, main circuit main
module main (
  input  w,
  input  reset,
  output A,
  output B,
  output C
);

  wire and_1_out, and_2_out, and_3_out, and_4_out, and_5_out, and_6_out, clock_1_out, not_1_out;

  and and_1 (and_1_out, ~A, B, C, w);  // AND_Gate
  and and_2 (and_2_out, A, B, C, w);
  and and_3 (and_3_out, ~B, C, w);  // AND_Gate
  and and_4 (and_4_out, B, C, w);
  and and_5 (and_5_out, ~C, w);  // AND_Gate
  and and_6 (and_6_out, C, w);
  Clock clock_1 (.out(clock_1_out));
  J_K_Flip_Flop JKA (.J(and_1_out), .K(and_2_out), .clk(clock_1_out), .Q(A), .reset(not_1_out));  // open: Qn, preset
  J_K_Flip_Flop JKB (.J(and_3_out), .K(and_4_out), .clk(clock_1_out), .Q(B), .reset(not_1_out));  // open: Qn, preset
  J_K_Flip_Flop JKC (.J(and_5_out), .K(and_6_out), .clk(clock_1_out), .Q(C), .reset(not_1_out));  // open: Qn, preset
  not not_1 (not_1_out, reset);
endmodule
