// Logisim project circuito.circ as structural Verilog: 2 circuits, main circuit circ_controle
module circ_controle (
  input  CLOCK,
  input  w,
  output C1,
  output H1,
  output C2,
  output H2,
  output C3,
  output H3,
  output DONE
);

  wire and_1_out, and_2_out, and_3_out, JKA_q, JKB_q;

  and and_1 (and_1_out, ~JKA_q, JKB_q);  // AND_Gate
  and and_2 (and_2_out, JKA_q, ~JKB_q);  // AND_Gate
  and and_3 (and_3_out, JKA_q, JKB_q);
  J_K_Flip_Flop JKA (.J(and_1_out), .K(and_2_out), .clk(CLOCK), .Q(JKA_q));  // open: Qn, preset, reset
  J_K_Flip_Flop JKB (.J(w), .K(and_3_out), .clk(CLOCK), .Q(JKB_q));  // open: Qn, preset, reset
  // AND_Gate A has open pins: in0=JKA_q, in1=JKB_q, out=open
  and B (C3, ~JKA_q, JKB_q);  // AND_Gate
  and C (C2, JKA_q, JKB_q);
  and D (C1, JKA_q, ~JKB_q);  // AND_Gate

  assign DONE = C1;
  assign H1 = C2;
  assign H2 = C3;
  assign H3 = C1;
endmodule

module main (
  input  w
);

  wire circ_controle_1_c1, circ_controle_1_c2, circ_controle_1_c3, circ_controle_1_done, circ_controle_1_h1,
       circ_controle_1_h2, circ_controle_1_h3, clock_1_out, controlled_buffer_1_out, R1_q, R2_q, R3_q;

  Clock clock_1 (.out(clock_1_out));
  circ_controle circ_controle_1 (
    .CLOCK(clock_1_out), .w(w), .C1(circ_controle_1_c1), .H1(circ_controle_1_h1), .C2(circ_controle_1_c2),
    .H2(circ_controle_1_h2), .C3(circ_controle_1_c3), .H3(circ_controle_1_h3), .DONE(circ_controle_1_done));
  Register #(.width(1)) R1 (
    .D(controlled_buffer_1_out), .en(circ_controle_1_c1), .clk(clock_1_out), .Q(R1_q));  // open: clr
  LED led_1 (.in(circ_controle_1_done));
  assign controlled_buffer_1_out = circ_controle_1_h1 ? R1_q : 1'bz;  // Controlled_Buffer controlled_buffer_1
  Register #(.width(1)) R2 (
    .D(controlled_buffer_1_out), .en(circ_controle_1_c2), .clk(clock_1_out), .Q(R2_q));  // open: clr
  assign controlled_buffer_1_out = circ_controle_1_h2 ? R2_q : 1'bz;  // Controlled_Buffer controlled_buffer_2
  Register #(.width(1)) R3 (
    .D(controlled_buffer_1_out), .en(circ_controle_1_c3), .clk(clock_1_out), .Q(R3_q));  // open: clr
  assign controlled_buffer_1_out = circ_controle_1_h3 ? R3_q : 1'bz;  // Controlled_Buffer controlled_buffer_3
endmodule
