// Logisim project circuito.circ as structural Verilog: 12 circuits, main circuit main
module main (
  input  [15:0] x,
  input  [15:0] c,
  input  [15:0] b,
  input  [15:0] a,
  input  in_5,
  input  in_6,
  output [3:0] Estado,
  output [15:0] out_8,
  output [15:0] out_9,
  output [1:0] out_10,
  output [1:0] out_11,
  output [1:0] out_12
);

  wire bc_1_done, bc_1_h, bc_1_lh, bc_1_ls, bc_1_lx, clock_1_out, not_1_out;

  Clock clock_1 (.out(clock_1_out));
  not not_1 (not_1_out, clock_1_out);
  LED led_1 (.in(bc_1_done));
  BC bc_1 (
    .clk(not_1_out), .rst(in_5), .Start(in_6), .Estado(Estado), .DONE(bc_1_done), .LX(bc_1_lx), .LS(bc_1_ls),
    .LH(bc_1_lh), .H(bc_1_h), .M0(out_10), .M1(out_11), .M2(out_12));
  BO bo_1 (
    .A(a), .B(b), .C(c), .X(x), .M0(out_10), .LX(bc_1_lx), .clk(not_1_out), .rst(in_5), .M2(out_12),
    .M1(out_11), .H(bc_1_h), .LS(bc_1_ls), .LH(bc_1_lh), .Reg2(out_8), .RESULTADO(out_9));
endmodule

module BO (
  input  [15:0] A,
  input  [15:0] B,
  input  [15:0] C,
  input  [15:0] X,
  input  [1:0] M0,
  input  LX,
  input  clk,
  input  rst,
  input  [1:0] M2,
  input  [1:0] M1,
  input  H,
  input  LS,
  input  LH,
  output [15:0] Reg2,
  output [15:0] RESULTADO
);

  wire [15:0] multiplexer_1_out, multiplexer_2_out, multiplexer_3_out, R0_q, somadormultiplicador_1_resultado;

  Register #(.width(16)) R0 (.D(X), .en(LX), .clk(clk), .Q(R0_q), .clr(rst));
  Register #(.width(16)) R1 (.D(somadormultiplicador_1_resultado), .en(LS), .clk(clk), .Q(RESULTADO), .clr(rst));
  Multiplexer #(.select(2), .width(16)) multiplexer_1 (
    .in0(R0_q), .in1(multiplexer_2_out), .in2(RESULTADO), .in3(Reg2), .out(multiplexer_1_out), .sel(M2));
  SomadorMultiplicador somadormultiplicador_1 (
    .A(multiplexer_3_out), .B(multiplexer_1_out), .entrada(H), .RESULTADO(somadormultiplicador_1_resultado));
  Register #(.width(16)) R2 (.D(somadormultiplicador_1_resultado), .en(LH), .clk(clk), .Q(Reg2), .clr(rst));
  Multiplexer #(.select(2), .width(16)) multiplexer_2 (
    .in1(A), .in2(B), .in3(C), .out(multiplexer_2_out), .sel(M0));  // open: in0
  Multiplexer #(.select(2), .width(16)) multiplexer_3 (
    .in0(R0_q), .in1(multiplexer_2_out), .in2(RESULTADO), .in3(Reg2), .out(multiplexer_3_out), .sel(M1));
endmodule

module BC (
  input  clk,
  input  rst,
  input  Start,
  output [3:0] Estado,
  output DONE,
  output LX,
  output LS,
  output LH,
  output H,
  output [1:0] M0,
  output [1:0] M1,
  output [1:0] M2
);

  wire B_out, C_out, D_out, E_out, F_out, G_out, Hs_out, I_out, J_out, ja_1_o, jb_1_o, jc_1_o, jd_1_o,
       ka_1_o, kb_1_o, kc_1_o, kd_1_o;

  JD jd_1 (.Y0(Estado[0]), .Y1(Estado[1]), .Y2(Estado[2]), .Y3(Estado[3]), .W(Start), .O(jd_1_o));
  KD kd_1 (.Y0(Estado[0]), .Y1(Estado[1]), .Y2(Estado[2]), .Y3(Estado[3]), .W(Start), .O(kd_1_o));
  J_K_Flip_Flop Y0 (.J(jd_1_o), .K(kd_1_o), .clk(clk), .Q(Estado[0]), .reset(rst));  // open: Qn, preset
  JC jc_1 (.Y0(Estado[0]), .Y1(Estado[1]), .Y2(Estado[2]), .Y3(Estado[3]), .W(Start), .O(jc_1_o));
  KC kc_1 (.Y0(Estado[0]), .Y1(Estado[1]), .Y2(Estado[2]), .Y3(Estado[3]), .W(Start), .O(kc_1_o));
  J_K_Flip_Flop Y1 (.J(jc_1_o), .K(kc_1_o), .clk(clk), .Q(Estado[1]), .reset(rst));  // open: Qn, preset
  JB jb_1 (.Y0(Estado[0]), .Y1(Estado[1]), .Y2(Estado[2]), .Y3(Estado[3]), .W(Start), .O(jb_1_o));
  KB kb_1 (.Y0(Estado[0]), .Y1(Estado[1]), .Y2(Estado[2]), .Y3(Estado[3]), .W(Start), .O(kb_1_o));
  J_K_Flip_Flop Y2 (.J(jb_1_o), .K(kb_1_o), .clk(clk), .Q(Estado[2]), .reset(rst));  // open: Qn, preset
  JA ja_1 (.Y0(Estado[0]), .Y1(Estado[1]), .Y2(Estado[2]), .Y3(Estado[3]), .W(Start), .O(ja_1_o));
  KA ka_1 (.Y0(Estado[0]), .Y1(Estado[1]), .Y2(Estado[2]), .Y3(Estado[3]), .W(Start), .O(ka_1_o));
  J_K_Flip_Flop Y3 (.J(ja_1_o), .K(ka_1_o), .clk(clk), .Q(Estado[3]), .reset(rst));  // open: Qn, preset
  and B (B_out, ~Estado[3], ~Estado[2], ~Estado[1], Estado[0]);  // AND_Gate
  or or_1 (LX, I_out, Hs_out, G_out, F_out, E_out, C_out, D_out, B_out, J_out, DONE);
  and C (C_out, ~Estado[3], ~Estado[2], Estado[1], ~Estado[0]);  // AND_Gate
  or or_2 (LS, DONE, G_out);
  and D (D_out, ~Estado[3], ~Estado[2], Estado[1], Estado[0]);  // AND_Gate
  and E (E_out, ~Estado[3], Estado[2], ~Estado[1], ~Estado[0]);  // AND_Gate
  or or_3 (LH, C_out, E_out, I_out);
  and F (F_out, ~Estado[3], Estado[2], ~Estado[1], Estado[0]);  // AND_Gate
  or or_4 (H, D_out, B_out, C_out, E_out, F_out, G_out);
  and G (G_out, ~Estado[3], Estado[2], Estado[1], ~Estado[0]);  // AND_Gate
  or or_5 (M0[1], DONE, J_out, G_out, F_out);
  and Hs (Hs_out, ~Estado[3], Estado[2], Estado[1], Estado[0]);  // AND_Gate
  and I (I_out, Estado[3], ~Estado[2], ~Estado[1], ~Estado[0]);  // AND_Gate
  or or_6 (M0[0], DONE, J_out, E_out, D_out);
  and J (J_out, Estado[3], ~Estado[2], ~Estado[1], Estado[0]);  // AND_Gate
  or or_7 (M1[1], I_out, Hs_out);
  and K (DONE, Estado[3], ~Estado[2], Estado[1], ~Estado[0]);  // AND_Gate
  or or_8 (M1[0], F_out, I_out, Hs_out, G_out, E_out, D_out, J_out, DONE);
  or or_9 (M2[1], I_out, Hs_out, DONE, E_out, D_out, J_out);
  or or_10 (M2[0], DONE, J_out, E_out, D_out);
endmodule

module SomadorMultiplicador (
  input  [15:0] A,
  input  [15:0] B,
  input  entrada,
  output [15:0] RESULTADO
);

  wire [15:0] adder_1_out, multiplier_1_out;

  Adder #(.width(16)) adder_1 (.a(A), .b(B), .out(adder_1_out));  // open: cin, cout
  Multiplier #(.width(16)) multiplier_1 (.a(A), .b(B), .out(multiplier_1_out));  // open: cin, cout
  Multiplexer #(.width(16)) multiplexer_1 (.in0(adder_1_out), .in1(multiplier_1_out), .out(RESULTADO), .sel(entrada));
endmodule

module JA (
  input  Y0,
  input  Y1,
  input  Y2,
  input  Y3,
  input  W,
  output O
);

  and and_1 (O, Y0, Y1, Y2, ~Y3);  // AND_Gate
endmodule

module KA (
  input  Y0,
  input  Y1,
  input  Y2,
  input  Y3,
  input  W,
  output O
);

  and and_1 (O, ~Y0, Y1, ~Y2, Y3);  // AND_Gate
endmodule

module JB (
  input  Y0,
  input  Y1,
  input  Y2,
  input  Y3,
  input  W,
  output O
);

  and and_1 (O, Y0, Y1, ~Y2, ~Y3);  // AND_Gate
endmodule

module KB (
  input  Y0,
  input  Y1,
  input  Y2,
  input  Y3,
  input  W,
  output O
);

  and and_1 (O, Y0, Y1, Y2, ~Y3);  // AND_Gate
endmodule

module JC (
  input  Y0,
  input  Y1,
  input  Y2,
  input  Y3,
  input  W,
  output O
);

  wire and_1_out, and_2_out, and_3_out;

  and and_1 (and_1_out, Y0, ~Y1, ~Y2, ~Y3);  // AND_Gate
  and and_2 (and_2_out, Y0, ~Y1, Y2, ~Y3);  // AND_Gate
  and and_3 (and_3_out, Y0, ~Y1, ~Y2, Y3);  // AND_Gate
  or or_1 (O, and_1_out, and_2_out, and_3_out);
endmodule

module KC (
  input  Y0,
  input  Y1,
  input  Y2,
  input  Y3,
  input  W,
  output O
);

  wire and_1_out, and_2_out, and_3_out;

  and and_1 (and_1_out, Y0, Y1, ~Y2, ~Y3);  // AND_Gate
  and and_2 (and_2_out, Y0, Y1, Y2, ~Y3);  // AND_Gate
  and and_3 (and_3_out, ~Y0, Y1, ~Y2, Y3);  // AND_Gate
  or or_1 (O, and_1_out, and_2_out, and_3_out);
endmodule

module JD (
  input  Y0,
  input  Y1,
  input  Y2,
  input  Y3,
  input  W,
  output O
);

  wire and_1_out, and_2_out, and_3_out, and_4_out, and_5_out;

  and and_1 (and_1_out, ~Y0, ~Y1, ~Y2, ~Y3, W);  // AND_Gate
  and and_2 (and_2_out, ~Y0, Y1, ~Y2, ~Y3);  // AND_Gate
  and and_3 (and_3_out, ~Y0, ~Y1, Y2, ~Y3);  // AND_Gate
  and and_4 (and_4_out, ~Y0, Y1, Y2, ~Y3);  // AND_Gate
  and and_5 (and_5_out, ~Y0, ~Y1, ~Y2, Y3);  // AND_Gate
  or or_1 (O, and_1_out, and_2_out, and_3_out, and_4_out, and_5_out);
endmodule

module KD (
  input  Y0,
  input  Y1,
  input  Y2,
  input  Y3,
  input  W,
  output O
);

  wire and_1_out, and_2_out, and_3_out, and_4_out, and_5_out;

  and and_1 (and_1_out, Y0, ~Y1, ~Y2, ~Y3);  // AND_Gate
  and and_2 (and_2_out, Y0, Y1, ~Y2, ~Y3);  // AND_Gate
  and and_3 (and_3_out, Y0, ~Y1, Y2, ~Y3);  // AND_Gate
  and and_4 (and_4_out, Y0, Y1, Y2, ~Y3);  // AND_Gate
  and and_5 (and_5_out, Y0, ~Y1, ~Y2, Y3);  // AND_Gate
  or or_1 (O, and_1_out, and_2_out, and_3_out, and_4_out, and_5_out);
endmodule
